# Fritzing sketch iAqua (saved by Fritzing 0.9.0b)
breadboards: 1
perfboards: 1

parts:
  Part1 = Arduino Mega 2560 (Rev3)
  BC337 = NPN-Transistor [package="TO92 [THT]"]
  IRFZ44N = Basic FET P-Channel [package="TO220 [THT]"]
  IRFZ44N_2 = Basic FET P-Channel [package="TO220 [THT]"]
  D1 = Rectifier Diode [part_number=1N4001 package="300 mil [THT]"]
  D2 = Rectifier Diode [part_number=1N4001 package="300 mil [THT]"]
  M1_(MACRO_PUMP) = DC Motor
  M2_(MICRO_PUMP) = DC Motor
  12V_POWER = Power plug
  D3 = LTE-302 [package=lte-302]
  RTC = DS1307 [package=so08]
  R4 = PHOTOCELL [package=photocell]
  DS18B20_Temp_Sensor = female pin header, 3 pins [form="♀ (female)"]
  R5 = Resistor [tolerance=±5% resistance=100 package="0603 [SMD]"]
  R1 = Resistor [tolerance=±5% resistance=1k package="1206 [SMD]"]
  R2 = Resistor [tolerance=±5% resistance=1k package="1206 [SMD]"]
  R3 = Resistor [tolerance=±5% resistance=150 package="1206 [SMD]"]
  R6 = Resistor [tolerance=±5% resistance=4.7k package="1206 [SMD]"]
  R7 = Resistor [tolerance=±5% resistance=1k package="1206 [SMD]"]
  W_LED = female pin header, 1 pin [form="♀ (female)"]
  G_LED = female pin header, 1 pin [form="♀ (female)"]
  B_LED = female pin header, 1 pin [form="♀ (female)"]
  R_LED = female pin header, 1 pin [form="♀ (female)"]
  RELAY = screw terminal, 10 pins
  J1 = female pin header, 20 pins [form="♀ (female)"]  # not connected
  IRFZ44N1 = Basic FET P-Channel [package="TO220 [THT]"]
  IRFZ44N2 = Basic FET P-Channel [package="TO220 [THT]"]
  R8 = Resistor [tolerance=±5% resistance=1k package="1206 [SMD]"]
  R9 = Resistor [tolerance=±5% resistance=1k package="1206 [SMD]"]
  D4 = Rectifier Diode [part_number=1N4001 package="300 mil [THT]"]
  D5 = Rectifier Diode [part_number=1N4001 package="300 mil [THT]"]
  L7805CV1 = Voltage Regulator - 5V [package="TO220 [THT]"]
  LCD_SCREEN = female pin header, 20 pins [form="♀ (female)"]
  C1 = Ceramic Capacitor [capacitance=470pF package="100 mil [THT, multilayer]"]
  MPX5700_PSI_Sensor = female pin header, 3 pins [form="♀ (female)"]
  RELAY1 = screw terminal, 10 pins

nets:
  N1: Part1.A8, R4.P$2, R5.Pin_1
  N2: Part1.A9, C1.1, MPX5700_PSI_Sensor.pin1
  N3: Part1.A0, RELAY.pin10
  N4: Part1.A1, RELAY.pin9
  N5: Part1.A2, RELAY.pin8
  N6: Part1.A3, RELAY.pin7
  N7: Part1.A4, RELAY.pin6
  N8: Part1.A5, RELAY.pin5
  N9: Part1.A6, RELAY.pin4
  N10: Part1.A7, RELAY.pin3
  N11: Part1.D21/SCL, Part1.SCL, RTC.SCL
  N12: Part1.D20/SDA, Part1.SDA, RTC.SDA
  N13: Part1.D11_PWM, R2.Pin_0
  N14: Part1.D10_PWM, R1.Pin_0
  N15: Part1.D9_PWM, D3.A
  N16: Part1.D8_PWM, R7.Pin_1
  5V: Part1.5V, BC337.C, RTC.VCC, R4.P$1, DS18B20_Temp_Sensor.pin1, R6.Pin_0, MPX5700_PSI_Sensor.pin2
  GND: Part1.GND, IRFZ44N.source, IRFZ44N_2.source, D1.anode, D2.anode, 12V_POWER.GND, RTC.GND, DS18B20_Temp_Sensor.pin2, R5.Pin_0, R3.Pin_1, RELAY.pin1, C1.0, MPX5700_PSI_Sensor.pin3
  VIN: Part1.VIN, M1_(MACRO_PUMP).pin_1, M2_(MICRO_PUMP).pin_1, 12V_POWER.VCC, RELAY.pin2
  N17: Part1.D4_PWM, R_LED.pin1
  N18: Part1.D5_PWM, G_LED.pin1
  N19: Part1.D6_PWM, B_LED.pin1
  N20: Part1.D7_PWM, W_LED.pin1
  N21: Part1.D47, DS18B20_Temp_Sensor.pin3, R6.Pin_1
  N22: BC337.E, LCD_SCREEN.pin2
  N23: BC337.B, R7.Pin_0
  N24: IRFZ44N.gate, R1.Pin_1
  N25: IRFZ44N.drain, D2.cathode, M1_(MACRO_PUMP).pin_2
  N26: IRFZ44N_2.gate, R2.Pin_1
  N27: IRFZ44N_2.drain, D1.cathode, M2_(MICRO_PUMP).pin_2
  N28: D3.C, R3.Pin_0
  N29: IRFZ44N1.gate, R8.Pin_1
  N30: IRFZ44N1.drain, D4.cathode, RELAY1.pin9
  N31: IRFZ44N1.source, D4.anode
  N32: IRFZ44N2.gate, R9.Pin_1
  N33: IRFZ44N2.drain, D5.cathode, RELAY1.pin7
  N34: IRFZ44N2.source, D5.anode
  N35: R8.Pin_0, RELAY1.pin10
  N36: R9.Pin_0, RELAY1.pin8
  N37: L7805CV1.input_voltage, RELAY1.pin1, RELAY1.pin3
  N38: L7805CV1.GND, RELAY1.pin2, RELAY1.pin4, RELAY1.pin6
  N39: L7805CV1.output_voltage, RELAY1.pin5

notes:
  AUX 2
  AUX 1
  CO2
  HEATER
  CIRC PUMP
  FILTER
  LIGHT 2
  LIGHT 1
  8 RELAY BOARD — 12V
  POWER SUPPLY — 12V
  To DS18B20 Temp Sensor
  PUMP 1 — MACROS
  PUMP 2 — MICROS
  IR LED
  IRFZ44N
  +12V
  GND
  R
  B
  G
  W
  BC337
  Light1
  Light2
  Filter
  Circ
  Heater
  Aux 1
  Aux 2
  +12v
  19 - LCD_BL
  20 - NOT USED
  21 - LCD_DB0
  22 - LCD_DB1
  23 - LCD_DB2
  24  - LCD_DB3
  25 - LCD_DB4
  26  - LCD_DB5
  27  - LCD_DB6
  28  - LCD_DB7
  29 - TouchP_CLK
  30 - TouchP_CS
  31 - TouchP_DIN
  32 - TouchP_BUSY
  33 - TouchP_OUT
  34 - TouchP_Penirq
  35 - SD_OUT
  36 - SD_SCK
  37 - SD_DIN
  38 - SD_CS
  39 - NOT USED
  40 - NOT USED
  3.2" TFT DISPLAY
  Arduino D10
  Macro Motor GND
  Arduino D11
  Micro Motor GND
  +12v OUT
  GND IN
  +12v IN
  GND OUT
  +5v OUT
  5- LCD_WR
  12 - LCD_DB13
  15 - LCD_CS
  6 - LCD_RD
  16 - NOT USED
  7 - LCD_DB8
  10 - LCD_DB11
  13 - LCD_DB14
  11 - LCD_DB12
  4 - LCD_RS
  14 - LCD_DB15
  2 - VCC
  9 - LCD_DB10
  3 - UNUSED
  18 - NOT USED
  1 - GND
  17 - LCD_RESET
  8 - LCD_DB9
  To MPX5700 Pressure Sensor
  470 pF
  TO R-G-B-W LED Channels if
  using DIY LEDs
